// Logisim project notgate.circ as structural Verilog
module main (
  input  a,
  output y
);

  not_gate U1 (.a(a), .y(y));
endmodule

// VHDL entity not_gate, as the project stores it:
library ieee;
use ieee.std_logic_1164.all;

entity not_gate is
    port (
        a : in  std_logic;
        y : out std_logic
    );
end not_gate;

architecture behavior of not_gate is
begin
    y <= not a;
end behavior;
